# Fritzing sketch CoderCompanion_IRsensor (saved by Fritzing 0.7.10b)
breadboards: 1

parts:
  J1 = Infrared Proximity Sensor
  S1 = Toggle Switch [package=THT]
  J2 = Basic Servo
  VCC1 = 4 x AAA Battery Mount
  Arduino1 = Arduino
  U2 = ATMEGA8U2 [package=tqfp]  # not connected
  U3 = atmega328 [package=dip]  # not connected

nets:
  N1: J1.Vout, Arduino1.A0
  GND: J1.GND, J2.gnd, Arduino1.GND
  N2: S1.L1, VCC1.+
  N3: S1.COM, J2.vcc
  N4: J2.pulse, Arduino1.D9
